// Logisim project Toilet_final.circ as structural Verilog
module main (
  input  in_1,
  input  in_2,
  input  in_3,
  input  in_4,
  input  in_5,
  input  in_6,
  input  in_7,
  input  in_8,
  input  in_9,
  input  in_10,
  input  in_11,
  input  in_12,
  input  in_13,
  input  in_14,
  input  in_15,
  input  [2:0] in_16,
  input  in_17,
  input  [2:0] in_18,
  input  in_19,
  input  [2:0] in_20,
  input  in_21,
  input  in_22,
  input  in_23,
  output out_24,
  output out_25,
  output out_26,
  output out_27,
  output [2:0] out_28,
  output out_29,
  output out_30,
  output out_31,
  output out_32,
  output out_33
);

  wire full_adder_1_cin_2, full_adder_1_s, full_adder_2_cin_2, full_adder_2_s, full_adder_3_cin_2,
       full_adder_3_s, full_adder_5_cin_2, full_adder_6_cin_2, full_adder_6_s, full_adder_7_cin_2,
       full_adder_7_s, full_adder_8_cin_2, full_adder_9_cin_2, full_adder_9_s, full_adder_10_cin_2,
       full_adder_10_s, full_adder_11_cin_2, full_adder_11_s, subtract_1_bout, subtract_2_bout,
       subtract_3_bout;
  wire [6:0] stage1_1_out_2, stage1_1_out_3, stage1_1_out_4, stage1_1_out_5, stage1_1_out_6, stage1_1_out_7,
       stage2_1_out_2, stage2_1_out_3, stage2_1_out_4, stage2_1_out_5, stage2_1_out_6, stage2_1_out_7,
       stage3_1_out_2, stage3_1_out_3, stage3_1_out_4, stage3_1_out_5, stage3_1_out_6, stage3_1_out_7;

  toilet toilet_1 ();
  toilet toilet_2 ();
  Full_Adder full_adder_1 (.A(in_2), .B(in_1), .Cin(in_3), .S(full_adder_1_s), .Cin_2(full_adder_1_cin_2));
  toilet toilet_3 ();
  toilet toilet_4 ();
  Full_Adder full_adder_2 (
    .A(full_adder_3_cin_2), .B(full_adder_1_cin_2), .Cin(full_adder_6_cin_2), .S(full_adder_2_s),
    .Cin_2(full_adder_2_cin_2));
  toilet toilet_5 ();
  Full_Adder full_adder_3 (.A(in_5), .B(in_4), .Cin(in_6), .S(full_adder_3_s), .Cin_2(full_adder_3_cin_2));
  Full_Adder full_adder_4 (
    .A(full_adder_7_cin_2), .B(full_adder_2_cin_2), .Cin(full_adder_5_cin_2), .S(out_25), .Cin_2(out_24));
  toilet toilet_6 ();
  Full_Adder full_adder_5 (
    .A(full_adder_7_s), .B(full_adder_2_s), .Cin(full_adder_8_cin_2), .S(out_26), .Cin_2(full_adder_5_cin_2));
  toilet toilet_7 ();
  toilet toilet_8 ();
  Full_Adder full_adder_6 (.A(in_8), .B(in_7), .Cin(in_9), .S(full_adder_6_s), .Cin_2(full_adder_6_cin_2));
  Full_Adder full_adder_7 (
    .A(full_adder_11_cin_2), .B(full_adder_10_cin_2), .Cin(full_adder_9_cin_2), .S(full_adder_7_s),
    .Cin_2(full_adder_7_cin_2));
  Full_Adder full_adder_8 (
    .A(full_adder_3_s), .B(full_adder_1_s), .Cin(full_adder_9_s), .S(out_27), .Cin_2(full_adder_8_cin_2));
  toilet toilet_9 ();
  subtract subtract_1 (.x(in_19), .y(out_24), .bin(in_17), .d(out_30), .bout(subtract_1_bout));
  subtract subtract_2 (.x(in_21), .y(out_25), .bin(subtract_1_bout), .d(out_31), .bout(subtract_2_bout));
  subtract subtract_3 (.x(in_22), .y(out_26), .bin(subtract_2_bout), .d(out_32), .bout(subtract_3_bout));
  subtract subtract_4 (.x(in_23), .y(out_27), .bin(subtract_3_bout), .d(out_33), .bout(out_29));
  toilet toilet_10 ();
  Full_Adder full_adder_9 (
    .A(full_adder_10_s), .B(full_adder_6_s), .Cin(full_adder_11_s), .S(full_adder_9_s),
    .Cin_2(full_adder_9_cin_2));
  toilet toilet_11 ();
  toilet toilet_12 ();
  Full_Adder full_adder_10 (.A(in_11), .B(in_10), .Cin(in_12), .S(full_adder_10_s), .Cin_2(full_adder_10_cin_2));
  Hex_Digit_Display hex_digit_display_1 (.value({out_24, out_25, out_26, out_27}));  // open: dp
  Hex_Digit_Display hex_digit_display_2 (.value({out_30, out_31, out_32, out_33}));  // open: dp
  toilet toilet_13 ();
  toilet toilet_14 ();
  Full_Adder full_adder_11 (.A(in_14), .B(in_13), .Cin(in_15), .S(full_adder_11_s), .Cin_2(full_adder_11_cin_2));
  toilet toilet_15 ();
  Multiplexer #(.select(4), .width(3)) multiplexer_1 (
    .in0(in_16), .in1(in_16), .in2(in_16), .in3(in_16), .in4(in_16), .in5(in_16), .in6(in_18), .in7(in_18),
    .in8(in_18), .in9(in_18), .in10(in_18), .in11(in_20), .in12(in_20), .in13(in_20), .in14(in_20),
    .in15(in_20), .out(out_28), .sel({out_24, out_25, out_26, out_27}));  // open: en
  Stage1 stage1_1 (
    .in_1(out_28[0]), .out_7(stage1_1_out_7), .out_6(stage1_1_out_6), .out_4(stage1_1_out_4),
    .out_3(stage1_1_out_3), .out_2(stage1_1_out_2), .out_5(stage1_1_out_5));
  Stage2 stage2_1 (
    .in_1(out_28[1]), .out_7(stage2_1_out_7), .out_6(stage2_1_out_6), .out_4(stage2_1_out_4),
    .out_3(stage2_1_out_3), .out_2(stage2_1_out_2), .out_5(stage2_1_out_5));
  Stage3 stage3_1 (
    .in_1(out_28[2]), .out_7(stage3_1_out_7), .out_6(stage3_1_out_6), .out_4(stage3_1_out_4),
    .out_3(stage3_1_out_3), .out_2(stage3_1_out_2), .out_5(stage3_1_out_5));
  DotMatrix #(.matrixcols(6)) dotmatrix_1 (
    .col0(stage1_1_out_7), .col1(stage1_1_out_6), .col2(stage1_1_out_4), .col3(stage1_1_out_3),
    .col4(stage1_1_out_2), .col5(stage1_1_out_5));
  DotMatrix #(.matrixcols(6)) dotmatrix_2 (
    .col0(stage2_1_out_7), .col1(stage2_1_out_6), .col2(stage2_1_out_4), .col3(stage2_1_out_3),
    .col4(stage2_1_out_2), .col5(stage2_1_out_5));
  DotMatrix #(.matrixcols(6)) dotmatrix_3 (
    .col0(stage3_1_out_7), .col1(stage3_1_out_6), .col2(stage3_1_out_4), .col3(stage3_1_out_3),
    .col4(stage3_1_out_2), .col5(stage3_1_out_5));

  // Notes on the sheet:
  //   Number of used room
  //   Number of room left
endmodule

module Full_Adder (
  input  A,
  input  B,
  input  Cin,
  output S,
  output Cin_2
);

  wire and_1_out, and_2_out, xor_1_out;

  xor xor_1 (xor_1_out, A, B);
  and and_1 (and_1_out, A, B);
  xor xor_2 (S, xor_1_out, Cin);
  and and_2 (and_2_out, xor_1_out, Cin);
  or or_1 (Cin_2, and_2_out, and_1_out);
endmodule

module decoder (
  input  [7:0] in_1
);

  wire [7:0] multiplexer_1_out;

  Hex_Digit_Display hex_digit_display_1 ();  // open: value, dp
  Multiplexer #(.select(4), .width(8)) multiplexer_1 (
    .in0(in_1), .out(multiplexer_1_out));  // open: in1, in2, in3, in4, in5, in6, in7, in8, in9, in10, in11, in12, in13, in14, in15, sel, en
endmodule

module IC (
  input  in_1,
  input  in_2,
  output [3:0] out_3
);


  assign out_3 = {{2{in_2}}, {2{in_1}}};
endmodule

module subtract (
  input  x,
  input  y,
  input  bin,
  output d,
  output bout
);

  wire and_1_out, and_2_out, not_1_out, not_2_out, xor_1_out;

  not not_1 (not_1_out, x);
  xor xor_1 (xor_1_out, x, y);
  and and_1 (and_1_out, not_1_out, y);
  not not_2 (not_2_out, xor_1_out);
  xor xor_2 (d, xor_1_out, bin);
  and and_2 (and_2_out, not_2_out, bin);
  or or_1 (bout, and_2_out, and_1_out);
endmodule

module Stage1 (
  input  in_1,
  output [6:0] out_2,
  output [6:0] out_3,
  output [6:0] out_4,
  output [6:0] out_5,
  output [6:0] out_6,
  output [6:0] out_7
);

  wire clock_1_out, not_1_out;

  Clock clock_1 (.out(clock_1_out));
  not not_1 (not_1_out, out_2[5]);
  and and_1 (out_5[4], not_1_out, in_1);
  D_Flip_Flop d_ff_1 (.clk(clock_1_out), .D(out_5[4]), .Q(out_2[5]));  // open: Qn, preset, en, reset

  assign {out_2[6], out_2[4:0]} = {in_1, 1'b0, in_1, 1'b0, {2{in_1}}};
  assign out_3 = {{5{in_1}}, 1'b0, in_1};
  assign out_4 = {{5{in_1}}, 1'b0, in_1};
  assign {out_5[6:5], out_5[3:0]} = {6{in_1}};
  assign out_6 = {in_1, out_2[5], 1'b0, in_1, 1'b0, {2{in_1}}};
  assign out_7 = {{2{in_1}}, out_5[4], {4{in_1}}};
endmodule

module Stage2 (
  input  in_1,
  output [6:0] out_2,
  output [6:0] out_3,
  output [6:0] out_4,
  output [6:0] out_5,
  output [6:0] out_6,
  output [6:0] out_7
);

  wire clock_1_out, not_1_out;

  Clock clock_1 (.out(clock_1_out));
  not not_1 (not_1_out, out_2[1]);
  and and_1 (out_5[4], not_1_out, in_1);
  D_Flip_Flop d_ff_1 (.clk(clock_1_out), .D(out_5[4]), .Q(out_2[1]));  // open: Qn, preset, en, reset

  assign {out_2[6:2], out_2[0]} = {{2{in_1}}, 1'b0, {3{in_1}}};
  assign out_3 = {{5{in_1}}, 1'b0, in_1};
  assign out_4 = {{5{in_1}}, 1'b0, in_1};
  assign {out_5[6:5], out_5[3:0]} = {6{in_1}};
  assign out_6 = {{2{in_1}}, 1'b0, {2{in_1}}, 1'b0, in_1};
  assign out_7 = {{2{in_1}}, out_5[4], {4{in_1}}};
endmodule

module Stage3 (
  input  in_1,
  output [6:0] out_2,
  output [6:0] out_3,
  output [6:0] out_4,
  output [6:0] out_5,
  output [6:0] out_6,
  output [6:0] out_7
);

  wire clock_1_out, not_1_out;

  Clock clock_1 (.out(clock_1_out));
  not not_1 (not_1_out, out_3[2]);
  and and_1 (out_3[1], not_1_out, in_1);
  D_Flip_Flop d_ff_1 (.clk(clock_1_out), .D(out_3[1]), .Q(out_3[2]));  // open: Qn, preset, en, reset

  assign out_2 = {{2{in_1}}, 1'b0, {2{in_1}}, 1'b0, in_1};
  assign {out_3[6:3], out_3[0]} = {5{in_1}};
  assign out_4 = {{4{in_1}}, out_3[2:1], in_1};
  assign out_5 = {in_1, out_3[2:1], {4{in_1}}};
  assign out_6 = {{2{in_1}}, 1'b0, {2{in_1}}, 1'b0, in_1};
  assign out_7 = {in_1, out_3[2:1], {4{in_1}}};
endmodule

module Stage1_flipflop (
);

  D_Flip_Flop d_ff_1 ();  // open: clk, D, Q, Qn, preset, en, reset
endmodule
